// Logisim project project.circ as structural Verilog: 19 circuits, main circuit main
module main (
  output [1:0] out_1,
  output [1:0] out_2,
  output [1:0] out_3
);

  wire abiEntrata, abiUscita, and_3_out, clock_1_out, entrata, luceRossa, luceVerde,
       macchina_principale_1_output_funzione, not_1_out, or_1_out, reset, sbarraEntrata, sbarraUscita, uscita;
  wire [1:0] selettore_1_output, selettore_iniziale_1_out_3;
  wire [3:0] macchina_principale_1_stato_attuale, sottraendo_1_out_1, sottrazione_complemento_a_2_1_risultato;

  Button button_1 (.out(reset));
  Button button_2 (.out(entrata));
  Button button_3 (.out(uscita));
  selettore_iniziale selettore_iniziale_1 (.\input (out_1), .in_2(or_1_out), .out_3(selettore_iniziale_1_out_3));
  macchina_principale macchina_principale_1 (
    .\input (selettore_iniziale_1_out_3), .tasto_reset(reset), .clock(or_1_out),
    .output_funzione(macchina_principale_1_output_funzione),
    .stato_attuale(macchina_principale_1_stato_attuale));
  registro_contenenti_i_valori_di_input registro_contenenti_i_valori_di_input_1 (
    .selettore_ingresso_uscita(selettore_1_output), .clock__collegato_al_reset(reset), .out_3(out_1));
  selettore selettore_1 (
    .registro_entrata(out_3), .registro_uscita(out_2), .entrata(entrata), .uscita(sbarraUscita),
    .\output (selettore_1_output));
  estensione_bit_uscita estensione_bit_uscita_1 (.in_1(sbarraUscita), .out_2(out_2));
  estensione_bit_entrata estensione_bit_entrata_1 (.in_1(sbarraEntrata), .out_2(out_3));
  sottraendo sottraendo_1 (.out_1(sottraendo_1_out_1));
  sottrazione_complemento_a_2 sottrazione_complemento_a_2_1 (
    .sottraendo(sottraendo_1_out_1), .minuendo(macchina_principale_1_stato_attuale),
    .risultato(sottrazione_complemento_a_2_1_risultato));
  Clock clock_1 (.out(clock_1_out));
  Demultiplexer demultiplexer_1 (
    .out0(luceVerde), .out1(luceRossa), .in(1'b1), .sel(macchina_principale_1_output_funzione));  // open: en
  or or_1 (or_1_out, sbarraUscita, entrata);
  and and_1 (sbarraEntrata, entrata, abiEntrata);
  and and_2 (sbarraUscita, abiUscita, uscita);
  LED led_1 (.in(abiEntrata));
  LED led_2 (.in(sbarraEntrata));
  LED led_3 (.in(abiUscita));
  LED led_4 (.in(sbarraUscita));
  not not_1 (not_1_out, luceRossa);
  Hex_Digit_Display hex_digit_display_1 (.value(sottrazione_complemento_a_2_1_risultato), .dp(clock_1_out));
  _7_Segment_Display u_7_segment_display_1 (.f(luceVerde), .e(luceVerde), .d(luceVerde));  // open: g, a, b, c, dp
  and and_3 (and_3_out, luceRossa, clock_1_out);
  _7_Segment_Display u_7_segment_display_2 (
    .f(and_3_out), .a(and_3_out), .b(and_3_out), .e(and_3_out), .d(and_3_out), .c(and_3_out));  // open: g, dp
  _7_Segment_Display u_7_segment_display_3 (.b(1'b1), .c(1'b1));  // open: g, f, a, e, d, dp
  _7_Segment_Display u_7_segment_display_4 (.g(1'b1), .b(1'b1), .e(1'b1), .d(1'b1), .c(1'b1));  // open: f, a, dp
  _7_Segment_Display u_7_segment_display_5 (.b(luceVerde), .c(luceVerde));  // open: g, f, a, e, d, dp
  _7_Segment_Display u_7_segment_display_6 (
    .g(luceVerde), .f(luceVerde), .e(luceVerde), .d(luceVerde), .c(luceVerde));  // open: a, b, dp
  _7_Segment_Display u_7_segment_display_7 (
    .f(and_3_out), .a(and_3_out), .e(and_3_out), .d(and_3_out));  // open: g, b, c, dp
  _7_Segment_Display u_7_segment_display_8 (
    .f(and_3_out), .a(and_3_out), .e(and_3_out), .d(and_3_out));  // open: g, b, c, dp
  and and_4 (abiEntrata, luceVerde, not_1_out);
  or or_2 (abiUscita, luceVerde, luceRossa);
  LED led_5 (.in(luceRossa));
  LED led_6 (.in(luceVerde));
  _7_Segment_Display u_7_segment_display_9 (.g(1'b1), .f(1'b1), .a(1'b1), .d(1'b1), .c(1'b1));  // open: b, e, dp
  _7_Segment_Display u_7_segment_display_10 (.g(1'b1), .f(1'b1), .a(1'b1), .b(1'b1), .e(1'b1));  // open: d, c, dp
  _7_Segment_Display u_7_segment_display_11 (.g(luceVerde), .e(luceVerde));  // open: f, a, b, d, c, dp
  _7_Segment_Display u_7_segment_display_12 (
    .g(luceVerde), .f(luceVerde), .a(luceVerde), .e(luceVerde), .d(luceVerde));  // open: b, c, dp
  _7_Segment_Display u_7_segment_display_13 (
    .g(and_3_out), .f(and_3_out), .a(and_3_out), .b(and_3_out), .e(and_3_out));  // open: d, c, dp
  _7_Segment_Display u_7_segment_display_14 (
    .f(and_3_out), .b(and_3_out), .e(and_3_out), .d(and_3_out), .c(and_3_out));  // open: g, a, dp
  _7_Segment_Display u_7_segment_display_15 (.f(1'b1), .a(1'b1), .b(1'b1), .e(1'b1), .c(1'b1));  // open: g, d, dp
  _7_Segment_Display u_7_segment_display_16 (
    .f(1'b1), .a(1'b1), .b(1'b1), .e(1'b1), .d(1'b1), .c(1'b1));  // open: g, dp
  _7_Segment_Display u_7_segment_display_17 (
    .f(luceVerde), .a(luceVerde), .b(luceVerde), .e(luceVerde), .d(luceVerde), .c(luceVerde));  // open: g, dp
  _7_Segment_Display u_7_segment_display_18 (
    .g(and_3_out), .f(and_3_out), .a(and_3_out), .b(and_3_out), .e(and_3_out), .c(and_3_out));  // open: d, dp
  _7_Segment_Display u_7_segment_display_19 (
    .g(and_3_out), .f(and_3_out), .e(and_3_out), .d(and_3_out));  // open: a, b, c, dp
  _7_Segment_Display u_7_segment_display_20 (.g(1'b1), .f(1'b1), .e(1'b1), .d(1'b1), .c(1'b1));  // open: a, b, dp
  _7_Segment_Display u_7_segment_display_21 (.b(1'b1), .c(1'b1));  // open: g, f, a, e, d, dp
  _7_Segment_Display u_7_segment_display_22 (
    .f(and_3_out), .a(and_3_out), .b(and_3_out), .e(and_3_out), .d(and_3_out), .c(and_3_out));  // open: g, dp
  _7_Segment_Display u_7_segment_display_23 (.b(1'b1), .c(1'b1));  // open: g, f, a, e, d, dp
  _7_Segment_Display u_7_segment_display_24 (.f(1'b1), .e(1'b1), .d(1'b1));  // open: g, a, b, c, dp
  _7_Segment_Display u_7_segment_display_25 (.b(1'b1), .c(1'b1));  // open: g, f, a, e, d, dp
endmodule

module flip_flop (
  input  bit_da_salvare,
  input  clock,
  output bit_ok,
  output out_4
);

  wire and_1_out, and_2_out, and_3_out, and_4_out, nor_1_out, nor_2_out, not_1_out, not_2_out;

  not not_1 (not_1_out, bit_da_salvare);
  and and_1 (and_1_out, bit_da_salvare, clock);
  and and_2 (and_2_out, not_1_out, clock);
  nor nor_1 (nor_1_out, and_1_out, nor_2_out);
  nor nor_2 (nor_2_out, nor_1_out, and_2_out);
  not not_2 (not_2_out, clock);
  and and_3 (and_3_out, nor_1_out, not_2_out);
  and and_4 (and_4_out, not_2_out, nor_2_out);
  nor nor_3 (bit_ok, and_3_out, out_4);
  nor nor_4 (out_4, bit_ok, and_4_out);
endmodule

module full_adder (
  input  \bit ,
  input  bit_2,
  input  riporto_in_ingresso,
  output bit_di_somma,
  output bit_di_riporto
);

  wire and_1_out, and_2_out, and_3_out, and_4_out, not_1_out, xnor_1_out, xor_1_out, xor_2_out;

  xnor xnor_1 (xnor_1_out, \bit , bit_2);
  xor xor_1 (xor_1_out, \bit , bit_2);
  not not_1 (not_1_out, riporto_in_ingresso);
  xor xor_2 (xor_2_out, \bit , bit_2);
  and and_1 (and_1_out, xnor_1_out, riporto_in_ingresso);
  and and_2 (and_2_out, xor_1_out, not_1_out);
  and and_3 (and_3_out, xor_2_out, riporto_in_ingresso);
  and and_4 (and_4_out, \bit , bit_2);
  or or_1 (bit_di_riporto, and_3_out, and_4_out);
  or or_2 (bit_di_somma, and_1_out, and_2_out);
endmodule

module sommatore_a_4_bit (
  input  [3:0] sottraendo,
  input  [3:0] minuendo,
  output riporto,
  output [3:0] calcolo
);

  wire full_adder_1_bit_di_riporto, full_adder_2_bit_di_riporto, full_adder_3_bit_di_riporto;

  full_adder full_adder_1 (
    .\bit (sottraendo[0]), .bit_2(minuendo[0]), .riporto_in_ingresso(1'b1), .bit_di_somma(calcolo[0]),
    .bit_di_riporto(full_adder_1_bit_di_riporto));
  full_adder full_adder_2 (
    .\bit (sottraendo[1]), .bit_2(minuendo[1]), .riporto_in_ingresso(full_adder_1_bit_di_riporto),
    .bit_di_somma(calcolo[1]), .bit_di_riporto(full_adder_2_bit_di_riporto));
  full_adder full_adder_3 (
    .\bit (sottraendo[2]), .bit_2(minuendo[2]), .riporto_in_ingresso(full_adder_2_bit_di_riporto),
    .bit_di_somma(calcolo[2]), .bit_di_riporto(full_adder_3_bit_di_riporto));
  full_adder full_adder_4 (
    .\bit (sottraendo[3]), .bit_2(minuendo[3]), .riporto_in_ingresso(full_adder_3_bit_di_riporto),
    .bit_di_somma(calcolo[3]), .bit_di_riporto(riporto));
endmodule

module sottrazione_complemento_a_2 (
  input  [3:0] sottraendo,
  input  [3:0] minuendo,
  output [3:0] risultato
);

  wire [3:0] not_1_out;

  not not_1 (not_1_out[0], minuendo[0]);
  not not_2 (not_1_out[1], minuendo[1]);
  not not_3 (not_1_out[2], minuendo[2]);
  not not_4 (not_1_out[3], minuendo[3]);
  sommatore_a_4_bit sommatore_a_4_bit_1 (
    .sottraendo(sottraendo), .minuendo(not_1_out), .calcolo(risultato));  // open: riporto

  // Notes on the sheet:
  //   il cambio bit l'ho messo nel circuito sommatore a 4 bit
  //   per questo progetto poi metterò il sottraendo a 9 fisso
  //   dato che i posti totali del parcheggio sono 9
endmodule

module registro_a_4_bit (
  input  [3:0] \input ,
  input  clock,
  output [3:0] \output 
);

  flip_flop flip_flop_1 (.bit_da_salvare(\input [0]), .clock(clock), .bit_ok(\output [0]));  // open: out_4
  flip_flop flip_flop_2 (.bit_da_salvare(\input [1]), .clock(clock), .bit_ok(\output [1]));  // open: out_4
  flip_flop flip_flop_3 (.bit_da_salvare(\input [2]), .clock(clock), .bit_ok(\output [2]));  // open: out_4
  flip_flop flip_flop_4 (.bit_da_salvare(\input [3]), .clock(clock), .bit_ok(\output [3]));  // open: out_4

  // Notes on the sheet:
  //   fatto a 4 bit per la complessità del mio progetto
endmodule

module x0_t_1 (
  input  x3,
  input  x2,
  input  x1,
  input  x0,
  input  i1,
  input  i0,
  output out_7
);

  wire and_1_out, and_2_out, and_3_out, and_4_out, and_5_out, and_6_out, and_7_out, and_8_out, and_9_out,
       and_10_out, and_11_out, and_12_out, and_13_out, and_14_out, not_1_out, not_2_out, not_3_out,
       not_4_out, not_5_out, not_6_out, not_7_out, not_8_out, not_9_out, not_10_out, not_11_out, not_12_out,
       not_13_out, not_14_out, not_15_out, not_16_out, not_17_out, not_18_out, not_19_out, or_1_out,
       or_2_out, or_3_out, or_4_out, xor_1_out;

  not not_1 (not_1_out, x3);
  not not_2 (not_2_out, x2);
  not not_3 (not_3_out, x1);
  not not_4 (not_4_out, x3);
  not not_5 (not_5_out, x2);
  not not_6 (not_6_out, x1);
  not not_7 (not_7_out, x2);
  not not_8 (not_8_out, x1);
  and and_1 (and_1_out, x3, not_2_out, not_3_out);
  not not_9 (not_9_out, x2);
  not not_10 (not_10_out, x1);
  not not_11 (not_11_out, x3);
  xor xor_1 (xor_1_out, x2, x1);
  and and_2 (and_2_out, not_4_out, x2, x1);
  and and_3 (and_3_out, x3, not_5_out, not_6_out);
  not not_12 (not_12_out, x3);
  and and_4 (and_4_out, not_12_out, x0);
  and and_5 (and_5_out, x3, not_7_out, not_8_out, x0);
  or or_1 (or_1_out, not_1_out, and_1_out);
  not not_13 (not_13_out, x3);
  not not_14 (not_14_out, x0);
  and and_6 (and_6_out, not_11_out, xor_1_out);
  not not_15 (not_15_out, x0);
  not not_16 (not_16_out, i0);
  and and_7 (and_7_out, or_1_out, x0);
  not not_17 (not_17_out, i1);
  and and_8 (and_8_out, not_13_out, not_14_out);
  and and_9 (and_9_out, x3, not_9_out, not_10_out);
  not not_18 (not_18_out, i1);
  or or_2 (or_2_out, and_6_out, and_2_out, and_3_out);
  or or_3 (or_3_out, and_4_out, and_5_out);
  not not_19 (not_19_out, i0);
  and and_10 (and_10_out, or_2_out, not_15_out);
  and and_11 (and_11_out, and_7_out, not_17_out, not_19_out);
  or or_4 (or_4_out, and_8_out, and_9_out);
  and and_12 (and_12_out, or_4_out, not_18_out, i0);
  and and_13 (and_13_out, and_10_out, i1, not_16_out);
  and and_14 (and_14_out, or_3_out, i1, i0);
  or or_5 (out_7, and_11_out, and_12_out, and_13_out, and_14_out);
endmodule

module x1_t_1 (
  input  x3,
  input  x2,
  input  x1,
  input  x0,
  input  i1,
  input  i0,
  output out_7
);

  wire and_1_out, and_2_out, and_3_out, and_4_out, and_5_out, and_6_out, and_7_out, and_8_out, not_1_out,
       not_2_out, not_3_out, not_4_out, not_5_out, not_6_out, not_7_out, not_8_out, not_9_out, not_10_out,
       not_11_out, not_12_out, not_13_out, not_14_out, not_15_out, not_16_out, or_1_out, xor_1_out;

  not not_1 (not_1_out, x3);
  not not_2 (not_2_out, i1);
  not not_3 (not_3_out, i0);
  not not_4 (not_4_out, x3);
  xor xor_1 (xor_1_out, x1, x0);
  not not_5 (not_5_out, i1);
  not not_6 (not_6_out, x3);
  not not_7 (not_7_out, x2);
  not not_8 (not_8_out, x3);
  not not_9 (not_9_out, x1);
  not not_10 (not_10_out, x0);
  not not_11 (not_11_out, x3);
  not not_12 (not_12_out, x2);
  not not_13 (not_13_out, x1);
  not not_14 (not_14_out, x0);
  not not_15 (not_15_out, x3);
  and and_1 (and_1_out, not_1_out, x1, not_2_out, not_3_out);
  and and_2 (and_2_out, not_6_out, not_7_out, x1, x0);
  and and_3 (and_3_out, not_8_out, x2, not_9_out, not_10_out);
  and and_4 (and_4_out, not_11_out, x2, x1, x0);
  and and_5 (and_5_out, x3, not_12_out, not_13_out, not_14_out);
  and and_6 (and_6_out, not_15_out, x1, i1, i0);
  and and_7 (and_7_out, not_4_out, xor_1_out, not_5_out, i0);
  or or_1 (or_1_out, and_2_out, and_3_out, and_4_out, and_5_out);
  not not_16 (not_16_out, i0);
  and and_8 (and_8_out, or_1_out, i1, not_16_out);
  or or_2 (out_7, and_1_out, and_7_out, and_8_out, and_6_out);
endmodule

module x2_t_1 (
  input  x3,
  input  x2,
  input  x1,
  input  x0,
  input  i1,
  input  i0,
  output out_7
);

  wire and_1_out, and_2_out, and_3_out, and_4_out, and_5_out, and_6_out, and_7_out, and_8_out, and_9_out,
       and_10_out, not_1_out, not_2_out, not_3_out, not_4_out, not_5_out, not_6_out, not_7_out, not_8_out,
       not_9_out, not_10_out, not_11_out, not_12_out, not_13_out, not_14_out, not_15_out, not_16_out,
       not_17_out, not_18_out, or_1_out, or_2_out;

  not not_1 (not_1_out, x3);
  not not_2 (not_2_out, i1);
  not not_3 (not_3_out, i0);
  and and_1 (and_1_out, not_1_out, x2, not_2_out, not_3_out);
  not not_4 (not_4_out, x3);
  and and_2 (and_2_out, not_4_out, not_5_out, x1, x0);
  not not_5 (not_5_out, x2);
  not not_6 (not_6_out, x3);
  and and_3 (and_3_out, not_6_out, x2, not_7_out);
  not not_7 (not_7_out, x1);
  not not_8 (not_8_out, x3);
  and and_4 (and_4_out, not_8_out, x2, x1, not_9_out);
  not not_9 (not_9_out, x0);
  not not_10 (not_10_out, i1);
  not not_11 (not_11_out, x3);
  and and_5 (and_5_out, not_11_out, x2, not_12_out, x0);
  not not_12 (not_12_out, x1);
  not not_13 (not_13_out, x3);
  and and_6 (and_6_out, not_13_out, x2, x1);
  not not_14 (not_14_out, x2);
  not not_15 (not_15_out, x1);
  and and_7 (and_7_out, x3, not_14_out, not_15_out, not_16_out);
  not not_16 (not_16_out, x0);
  not not_17 (not_17_out, x3);
  and and_8 (and_8_out, not_17_out, x2, i1, i0);
  or or_1 (or_1_out, and_2_out, and_3_out, and_4_out);
  or or_2 (or_2_out, and_5_out, and_6_out, and_7_out);
  not not_18 (not_18_out, i0);
  and and_9 (and_9_out, or_1_out, not_10_out, i0);
  and and_10 (and_10_out, or_2_out, i1, not_18_out);
  or or_3 (out_7, and_1_out, and_9_out, and_10_out, and_8_out);
endmodule

module x3_t_1 (
  input  x3,
  input  x2,
  input  x1,
  input  x0,
  input  i1,
  input  i0,
  output out_7
);

  wire and_1_out, and_2_out, and_3_out, and_4_out, and_5_out, and_6_out, not_1_out, not_2_out, not_3_out,
       not_4_out, not_5_out, not_6_out, not_7_out, not_8_out, not_9_out, not_10_out, not_11_out, not_12_out,
       not_13_out, or_1_out;

  not not_1 (not_1_out, x2);
  not not_2 (not_2_out, x1);
  not not_3 (not_3_out, i1);
  not not_4 (not_4_out, i0);
  not not_5 (not_5_out, x3);
  not not_6 (not_6_out, x2);
  not not_7 (not_7_out, x1);
  not not_8 (not_8_out, x2);
  not not_9 (not_9_out, x1);
  not not_10 (not_10_out, i0);
  and and_1 (and_1_out, x3, not_1_out, not_2_out, not_3_out, not_4_out);
  and and_2 (and_2_out, not_5_out, x2, x1, x0);
  and and_3 (and_3_out, x3, not_6_out, not_7_out);
  and and_4 (and_4_out, x3, not_8_out, not_9_out, x0, i1, not_10_out);
  not not_11 (not_11_out, x2);
  and and_5 (and_5_out, x3, not_11_out, not_12_out, i1, i0);
  not not_12 (not_12_out, x1);
  or or_1 (or_1_out, and_2_out, and_3_out);
  not not_13 (not_13_out, i1);
  and and_6 (and_6_out, or_1_out, not_13_out, i0);
  or or_2 (out_7, and_1_out, and_6_out, and_4_out, and_5_out);
endmodule

module reset (
  input  bit_normale,
  input  reset,
  output out_3
);

  wire multiplexer_1_out;

  Multiplexer multiplexer_1 (.in1(1'b0), .out(multiplexer_1_out), .sel(reset));  // open: in0, en
  Multiplexer multiplexer_2 (.in0(bit_normale), .in1(multiplexer_1_out), .out(out_3), .sel(reset));  // open: en
endmodule

module macchina_principale (
  input  [1:0] \input ,
  input  tasto_reset,
  input  clock,
  output output_funzione,
  output [3:0] stato_attuale
);

  wire multiplexer_1_out, not_1_out, not_2_out, x0_t_1_1_out_7, x1_t_1_1_out_7, x2_t_1_1_out_7,
       x3_t_1_1_out_7;
  wire [3:0] reset_3_out_3;

  x0_t_1 x0_t_1_1 (
    .x3(stato_attuale[3]), .x2(stato_attuale[2]), .x1(stato_attuale[1]), .x0(stato_attuale[0]),
    .i1(\input [1]), .i0(\input [0]), .out_7(x0_t_1_1_out_7));
  x1_t_1 x1_t_1_1 (
    .x3(stato_attuale[3]), .x2(stato_attuale[2]), .x1(stato_attuale[1]), .x0(stato_attuale[0]),
    .i1(\input [1]), .i0(\input [0]), .out_7(x1_t_1_1_out_7));
  x2_t_1 x2_t_1_1 (
    .x3(stato_attuale[3]), .x2(stato_attuale[2]), .x1(stato_attuale[1]), .x0(stato_attuale[0]),
    .i1(\input [1]), .i0(\input [0]), .out_7(x2_t_1_1_out_7));
  x3_t_1 x3_t_1_1 (
    .x3(stato_attuale[3]), .x2(stato_attuale[2]), .x1(stato_attuale[1]), .x0(stato_attuale[0]),
    .i1(\input [1]), .i0(\input [0]), .out_7(x3_t_1_1_out_7));
  not not_1 (not_1_out, stato_attuale[2]);
  not not_2 (not_2_out, stato_attuale[1]);
  and and_1 (output_funzione, stato_attuale[3], not_1_out, not_2_out, stato_attuale[0]);
  reset reset_1 (.bit_normale(x2_t_1_1_out_7), .reset(tasto_reset), .out_3(reset_3_out_3[2]));
  reset reset_2 (.bit_normale(x3_t_1_1_out_7), .reset(tasto_reset), .out_3(reset_3_out_3[3]));
  registro_a_4_bit registro_a_4_bit_1 (.\input (reset_3_out_3), .clock(multiplexer_1_out), .\output (stato_attuale));
  reset reset_3 (.bit_normale(x0_t_1_1_out_7), .reset(tasto_reset), .out_3(reset_3_out_3[0]));
  reset reset_4 (.bit_normale(x1_t_1_1_out_7), .reset(tasto_reset), .out_3(reset_3_out_3[1]));
  Multiplexer multiplexer_1 (.in0(clock), .in1(tasto_reset), .out(multiplexer_1_out), .sel(tasto_reset));  // open: en
endmodule

module sottraendo (
  output [3:0] out_1
);


  assign out_1 = 4'b1001;
endmodule

module selettore_iniziale (
  input  [1:0] \input ,
  input  in_2,
  output [1:0] out_3
);

  Multiplexer #(.width(2)) multiplexer_1 (.in0(2'b00), .in1(\input ), .out(out_3), .sel(in_2));  // open: en
endmodule

module registro_contenenti_i_valori_di_input (
  input  [1:0] selettore_ingresso_uscita,
  input  clock__collegato_al_reset,
  output [1:0] out_3
);

  wire [1:0] registro_a_2_bit_1_out_3, registro_a_2_bit_2_out_3, registro_a_2_bit_3_out_3,
       registro_a_2_bit_4_out_3;

  registro_a_2_bit registro_a_2_bit_1 (
    .\input (2'b00), .clock(clock__collegato_al_reset), .out_3(registro_a_2_bit_1_out_3));
  registro_a_2_bit registro_a_2_bit_2 (
    .\input (2'b01), .clock(clock__collegato_al_reset), .out_3(registro_a_2_bit_2_out_3));
  registro_a_2_bit registro_a_2_bit_3 (
    .\input (2'b10), .clock(clock__collegato_al_reset), .out_3(registro_a_2_bit_3_out_3));
  registro_a_2_bit registro_a_2_bit_4 (
    .\input (2'b11), .clock(clock__collegato_al_reset), .out_3(registro_a_2_bit_4_out_3));
  Multiplexer #(.select(2), .width(2)) multiplexer_1 (
    .in0(registro_a_2_bit_1_out_3), .in1(registro_a_2_bit_2_out_3), .in2(registro_a_2_bit_3_out_3),
    .in3(registro_a_2_bit_4_out_3), .out(out_3), .sel(selettore_ingresso_uscita));  // open: en
endmodule

module registro_a_2_bit (
  input  [1:0] \input ,
  input  clock,
  output [1:0] out_3
);

  flip_flop flip_flop_1 (.bit_da_salvare(\input [0]), .clock(clock), .bit_ok(out_3[0]));  // open: out_4
  flip_flop flip_flop_2 (.bit_da_salvare(\input [1]), .clock(clock), .bit_ok(out_3[1]));  // open: out_4
endmodule

module estensione_bit_entrata (
  input  in_1,
  output [1:0] out_2
);

  assign out_2 = {{1{1'b0}}, in_1};  // Bit_Extender bit_extender_1
endmodule

module estensione_bit_uscita (
  input  in_1,
  output [1:0] out_2
);

  wire not_1_out;

  not not_1 (not_1_out, in_1);
  assign out_2 = {{1{1'b1}}, not_1_out};  // Bit_Extender bit_extender_1
endmodule

module selettore (
  input  [1:0] registro_entrata,
  input  [1:0] registro_uscita,
  input  entrata,
  input  uscita,
  output [1:0] \output 
);

  wire and_1_out, not_1_out, or_1_out;

  not not_1 (not_1_out, entrata);
  and and_1 (and_1_out, not_1_out, uscita);
  or or_1 (or_1_out, entrata, uscita);
  Multiplexer #(.width(2)) multiplexer_1 (
    .in0(registro_entrata), .in1(registro_uscita), .out(\output ), .sel(and_1_out), .en(or_1_out));
endmodule
